# Fritzing sketch bb1_hardware (saved by Fritzing 0.8.5b)
stripboards: 1

parts:
  Part1 = Arduino Leonardo (Rev3b)
  Raspberry_Pi_B_rev1 = Raspberry Pi B rev1  # not connected
  X1 = X113647 Stepper Driver Board [package=board]
  X2 = X113647 Stepper Driver Board [package=board]
  U1 = 74HC595 SMD [package="SO16 [SMD]"]
  U2 = V_REG_NCP50X [package=dpak-5]
  VCC2 = Battery
  VCC1 = Battery
  D1 = Rectifier Diode [part_number=1N4001 package="300 mil [THT]"]
  D2 = Rectifier Diode [part_number=1N4001 package="300 mil [THT]"]
  J1 = Basic Servo  # not connected
  J2 = Infrared Proximity Sensor  # not connected
  J3 = Infrared Proximity Sensor  # not connected

nets:
  N1: Part1.D7, U1.ST_CP
  5V: Part1.5V, U1.VCC
  GND: Part1.GND, X1.GND, X2.GND, U1.GND, U1.OE, U2.GND
  N2: Part1.VIN, X2.+V
  N3: Part1.D8/A8, U1.DS
  N4: Part1.D12/A11, U1.MR, U1.SH_CP
  N5: X1.IN1, U1.Q4
  N6: X1.IN2, U1.Q5
  N7: X1.IN3, U1.Q6
  N8: X1.IN4, U1.Q7
  N9: X1.+V, U2.EN
  N10: X2.IN1, U1.Q0
  N11: X2.IN2, U1.Q1
  N12: X2.IN3, U1.Q2
  N13: X2.IN4, U1.Q3
  N14: U2.IN, D1.cathode, D2.cathode
  N15: U2.OUT, VCC2.-, VCC1.-

custom parts:
  X113647 Stepper Driver Board: A common stepper motor driver board based on ULN2003APG darlington array
